// Logisim project watches_scheme.circ as structural Verilog: 6 circuits, main circuit main
module main (
);

  wire A, A_out, AB_out, and_1_out, and_2_out, and_3_out, and_4_out, and_5_out, and_6_out, and_7_out, B,
       B_out, controlled_buffer_1_out, controlled_buffer_2_out, controlled_buffer_15_out, gen, l1, l2, l3,
       l4, l5, l6, meridiem, not_2_out, not_3_out, or_1_out, or_2_out, or_5_out, q1, q2, q3, q4,
       signal_1_out_5, t_ff_1_q, xor_1_out, z1, z2, z3, z4, z5, z6, z7;
  wire [3:0] h_tens, h_units, min_tens, min_tens_swatch, min_units, min_units_swatch, sec_tens,
       sec_tens_swatch, sec_units, sec_units_swatch;
  wire [6:0] controlled_buffer_3_out, controlled_buffer_4_out, controlled_buffer_6_out,
       controlled_buffer_7_out, controlled_buffer_9_out, controlled_buffer_10_out, controlled_buffer_12_out,
       controlled_buffer_13_out, multiplexer_1_output, multiplexer_2_output, multiplexer_3_output,
       multiplexer_4_output, multiplexer_5_output, multiplexer_6_output, multiplexer_7_output,
       multiplexer_8_output;

  T_Flip_Flop t_ff_1 (.clk(or_1_out), .T(1'b1), .Q(t_ff_1_q));  // open: Qn, preset, reset, en
  or or_1 (or_1_out, and_1_out, z3);
  automata_main automata_main_1 (
    .A(A), .B(B), .q1(q1), .q2(q2), .q3(q3), .q4(q4), .q1_2(q1), .q2_2(q2), .q3_2(q3), .q4_2(q4), .z1(z1),
    .z2(z2), .z3(z3), .z4(z4), .z5(z5), .z6(z6), .z7(z7));
  not not_1 (meridiem, t_ff_1_q);
  Counter #(.width(4), .max('hf)) counter_1 (
    .Q(h_tens), .clk(and_2_out), .clr(and_1_out));  // open: load, D, count, carry
  and and_1 (and_1_out, h_tens[0], and_3_out);
  xor xor_1 (xor_1_out, and_1_out, and_2_out);
  assign controlled_buffer_1_out = l3 ? 1'b1 : 1'bz;  // Controlled_Buffer controlled_buffer_1
  _7_Segment_Display u_7_segment_display_1 (
    .g(controlled_buffer_1_out), .f(controlled_buffer_1_out), .a(controlled_buffer_1_out),
    .b(controlled_buffer_1_out), .e(controlled_buffer_1_out), .c(controlled_buffer_2_out));  // open: d, dp
  assign controlled_buffer_2_out = l3 ? meridiem : 1'bz;  // Controlled_Buffer controlled_buffer_2
  Counter #(.width(4), .max('hf)) counter_2 (
    .Q(h_units), .clk(or_2_out), .clr(xor_1_out));  // open: load, D, count, carry
  or or_2 (or_2_out, and_4_out, z2);
  multiplexer multiplexer_1 (.\input (min_tens_swatch), .\output (multiplexer_1_output));
  assign controlled_buffer_3_out = l5 ? multiplexer_1_output : 7'bz;  // Controlled_Buffer controlled_buffer_3
  and and_2 (and_2_out, h_units[1], h_units[3]);
  assign controlled_buffer_4_out = not_2_out ? controlled_buffer_3_out : 7'bz;  // Controlled_Buffer controlled_buffer_4
  assign controlled_buffer_3_out = l2 ? multiplexer_2_output : 7'bz;  // Controlled_Buffer controlled_buffer_5
  multiplexer multiplexer_2 (.\input (h_tens), .\output (multiplexer_2_output));
  and and_3 (and_3_out, ~h_units[0], h_units[1], ~h_units[2], ~h_units[3]);  // AND_Gate
  _7_Segment_Display u_7_segment_display_2 (
    .g(controlled_buffer_4_out[3]), .f(controlled_buffer_4_out[4]), .a(controlled_buffer_4_out[5]),
    .b(controlled_buffer_4_out[6]), .e(controlled_buffer_4_out[0]), .d(controlled_buffer_4_out[1]),
    .c(controlled_buffer_4_out[2]));  // open: dp
  Button u_A (.out(A_out));
  Button AB (.out(AB_out));
  Button u_B (.out(B_out));
  _7_Segment_Display u_7_segment_display_3 (
    .g(controlled_buffer_7_out[3]), .f(controlled_buffer_7_out[4]), .a(controlled_buffer_7_out[5]),
    .b(controlled_buffer_7_out[6]), .e(controlled_buffer_7_out[0]), .d(controlled_buffer_7_out[1]),
    .c(controlled_buffer_7_out[2]));  // open: dp
  or or_3 (A, A_out, AB_out);
  or or_4 (B, AB_out, B_out);
  Counter #(.width(4), .max('hf)) counter_3 (
    .Q(min_tens), .clk(and_5_out), .clr(and_4_out));  // open: load, D, count, carry
  multiplexer multiplexer_3 (.\input (min_units_swatch), .\output (multiplexer_3_output));
  assign controlled_buffer_6_out = l5 ? multiplexer_3_output : 7'bz;  // Controlled_Buffer controlled_buffer_6
  assign controlled_buffer_7_out = not_2_out ? controlled_buffer_6_out : 7'bz;  // Controlled_Buffer controlled_buffer_7
  assign controlled_buffer_6_out = l2 ? multiplexer_4_output : 7'bz;  // Controlled_Buffer controlled_buffer_8
  multiplexer multiplexer_4 (.\input (h_units), .\output (multiplexer_4_output));
  not not_2 (not_2_out, l6);
  and and_4 (and_4_out, min_tens[1], min_tens[2]);
  stopwatch stopwatch_1 (
    .state(l5), .reset(z6), .start_pause(z5), .generator(gen), .out_5(min_tens_swatch),
    .out_6(min_units_swatch), .out_7(sec_tens_swatch), .out_8(sec_units_swatch));
  multiplexer multiplexer_5 (.\input (sec_tens_swatch), .\output (multiplexer_5_output));
  assign controlled_buffer_9_out = l5 ? multiplexer_5_output : 7'bz;  // Controlled_Buffer controlled_buffer_9
  assign controlled_buffer_10_out = not_2_out ? controlled_buffer_9_out : 7'bz;  // Controlled_Buffer controlled_buffer_10
  assign controlled_buffer_9_out = l1 ? multiplexer_6_output : 7'bz;  // Controlled_Buffer controlled_buffer_11
  multiplexer multiplexer_6 (.\input (min_tens), .\output (multiplexer_6_output));
  LED led_1 (.in(signal_1_out_5));
  signal signal_1 (
    .sec_units(sec_units), .sec_tens(sec_tens), .min_units(min_units), .min_tens(min_tens),
    .out_5(signal_1_out_5));
  Counter #(.width(4), .max('hf)) counter_4 (
    .Q(min_units), .clk(or_5_out), .clr(and_5_out));  // open: load, D, count, carry
  or or_5 (or_5_out, and_6_out, z1);
  _7_Segment_Display u_7_segment_display_4 (
    .g(controlled_buffer_10_out[3]), .f(controlled_buffer_10_out[4]), .a(controlled_buffer_10_out[5]),
    .b(controlled_buffer_10_out[6]), .e(controlled_buffer_10_out[0]), .d(controlled_buffer_10_out[1]),
    .c(controlled_buffer_10_out[2]));  // open: dp
  and and_5 (and_5_out, min_units[1], min_units[3]);
  _7_Segment_Display u_7_segment_display_5 (
    .g(controlled_buffer_12_out[3]), .f(controlled_buffer_12_out[4]), .a(controlled_buffer_12_out[5]),
    .b(controlled_buffer_12_out[6]), .e(controlled_buffer_12_out[0]), .d(controlled_buffer_12_out[1]),
    .c(controlled_buffer_12_out[2]));  // open: dp
  Hex_Digit_Display hex_digit_display_1 (.value({q1, q2, q3, q4}));  // open: dp
  assign controlled_buffer_12_out = not_2_out ? controlled_buffer_13_out : 7'bz;  // Controlled_Buffer controlled_buffer_12
  Counter #(.width(4), .max('hf)) counter_5 (
    .Q(sec_tens), .clk(and_7_out), .clr(and_6_out));  // open: load, D, count, carry
  multiplexer multiplexer_7 (.\input (sec_units_swatch), .\output (multiplexer_7_output));
  assign controlled_buffer_13_out = l5 ? multiplexer_7_output : 7'bz;  // Controlled_Buffer controlled_buffer_13
  assign controlled_buffer_13_out = l1 ? multiplexer_8_output : 7'bz;  // Controlled_Buffer controlled_buffer_14
  multiplexer multiplexer_8 (.\input (min_units), .\output (multiplexer_8_output));
  and and_6 (and_6_out, sec_tens[1], sec_tens[2]);
  Clock clock_1 (.out(gen));
  assign controlled_buffer_15_out = not_3_out ? gen : 1'bz;  // Controlled_Buffer controlled_buffer_15
  not not_3 (not_3_out, l4);
  automata_states automata_states_1 (
    .q1(q1), .q2(q2), .q3(q3), .q4(q4), .l1(l1), .l2(l2), .l3(l3), .l4(l4), .l5(l5), .l6(l6));
  Counter #(.width(4), .max('hf)) counter_6 (
    .Q(sec_units), .clk(controlled_buffer_15_out), .clr(and_7_out));  // open: load, D, count, carry
  and and_7 (and_7_out, sec_units[1], sec_units[3]);
endmodule

// MUX
module multiplexer (
  input  [3:0] \input ,
  output [6:0] \output 
);

  wire and_1_out, and_2_out, and_3_out, and_4_out, and_5_out, and_6_out, and_7_out, and_8_out, and_9_out,
       and_10_out, and_11_out, and_12_out, and_13_out, and_14_out, and_15_out, and_16_out, and_17_out,
       and_18_out, and_19_out, and_20_out, and_21_out, and_22_out, and_23_out, and_24_out, and_25_out,
       and_26_out;

  and and_1 (and_1_out, ~\input [0], ~\input [1], ~\input [3]);  // AND_Gate
  and and_2 (and_2_out, \input [0], \input [1], ~\input [3]);  // AND_Gate
  and and_3 (and_3_out, ~\input [2], ~\input [3]);  // AND_Gate
  and and_4 (and_4_out, ~\input [1], ~\input [2]);  // AND_Gate
  and and_5 (and_5_out, ~\input [0], ~\input [2], ~\input [3]);  // AND_Gate
  and and_6 (and_6_out, ~\input [1], ~\input [2], \input [3]);  // AND_Gate
  and and_7 (and_7_out, \input [0], \input [2], ~\input [3]);  // AND_Gate
  and and_8 (and_8_out, \input [1], ~\input [3]);  // AND_Gate
  and and_9 (and_9_out, ~\input [0], ~\input [1], ~\input [3]);  // AND_Gate
  and and_10 (and_10_out, ~\input [1], ~\input [2], \input [3]);  // AND_Gate
  and and_11 (and_11_out, ~\input [1], \input [2], ~\input [3]);  // AND_Gate
  and and_12 (and_12_out, ~\input [0], \input [2], ~\input [3]);  // AND_Gate
  and and_13 (and_13_out, ~\input [1], ~\input [2], \input [3]);  // AND_Gate
  and and_14 (and_14_out, ~\input [1], \input [2], ~\input [3]);  // AND_Gate
  and and_15 (and_15_out, \input [1], ~\input [2], ~\input [3]);  // AND_Gate
  and and_16 (and_16_out, ~\input [0], \input [1], ~\input [3]);  // AND_Gate
  and and_17 (and_17_out, ~\input [0], \input [1], ~\input [3]);  // AND_Gate
  and and_18 (and_18_out, ~\input [0], ~\input [1], ~\input [2]);  // AND_Gate
  and and_19 (and_19_out, ~\input [0], \input [1], ~\input [3]);  // AND_Gate
  and and_20 (and_20_out, \input [1], ~\input [2], ~\input [3]);  // AND_Gate
  and and_21 (and_21_out, ~\input [1], ~\input [2], \input [3]);  // AND_Gate
  and and_22 (and_22_out, ~\input [0], ~\input [2], ~\input [3]);  // AND_Gate
  and and_23 (and_23_out, \input [0], ~\input [1], \input [2], ~\input [3]);  // AND_Gate
  and and_24 (and_24_out, \input [0], ~\input [3]);  // AND_Gate
  and and_25 (and_25_out, \input [2], ~\input [3]);  // AND_Gate
  and and_26 (and_26_out, ~\input [1], ~\input [2]);  // AND_Gate
  or or_1 (\output [6], and_1_out, and_2_out, and_3_out, and_4_out);
  or or_2 (\output [5], and_5_out, and_6_out, and_7_out, and_8_out);
  or or_3 (\output [4], and_9_out, and_10_out, and_11_out, and_12_out);
  or or_4 (\output [3], and_13_out, and_14_out, and_15_out, and_16_out);
  or or_5 (\output [2], and_24_out, and_25_out, and_26_out);
  or or_6 (\output [0], and_17_out, and_18_out);
  _7_Segment_Display u_7_segment_display_1 (
    .g(\output [3]), .f(\output [4]), .a(\output [5]), .b(\output [6]), .e(\output [0]), .d(\output [1]),
    .c(\output [2]));  // open: dp
  or or_7 (\output [1], and_19_out, and_20_out, and_21_out, and_22_out, and_23_out);
endmodule

// F
module automata_main (
  input  A,
  input  B,
  input  q1,
  input  q2,
  input  q3,
  input  q4,
  output q1_2,
  output q2_2,
  output q3_2,
  output q4_2,
  output z1,
  output z2,
  output z3,
  output z4,
  output z5,
  output z6,
  output z7
);

  wire and_1_out, and_2_out, and_3_out, and_4_out, and_5_out, and_6_out, and_7_out, and_8_out, and_9_out,
       and_10_out, and_11_out, and_12_out, and_13_out, and_14_out, and_15_out, and_16_out, and_17_out,
       and_21_out, and_22_out, and_23_out, and_24_out, and_25_out, and_26_out, and_27_out, and_28_out,
       and_29_out, and_30_out, and_31_out, and_32_out, and_33_out, and_34_out, and_35_out, not_1_out,
       not_2_out, or_1_out, Q1_out, Q2_out, Q3_out, Q4_out;

  or or_1 (or_1_out, A, B);
  not not_1 (not_1_out, or_1_out);
  and and_1 (and_1_out, ~A, B, ~q1, q2, q3);  // AND_Gate
  and and_2 (and_2_out, ~A, B, q1, ~q2, ~q3, ~q4);  // AND_Gate
  and and_3 (and_3_out, A, ~B, ~q1, q2, q3);  // AND_Gate
  and and_4 (and_4_out, A, ~q1, ~q2, q3, q4);  // AND_Gate
  and and_5 (and_5_out, B, ~q1, ~q2, ~q3, ~q4);  // AND_Gate
  and and_6 (and_6_out, A, ~B, q1, ~q2, ~q3, ~q4);  // AND_Gate
  and and_7 (and_7_out, A, ~B, ~q1, q2, q3);  // AND_Gate
  and and_8 (and_8_out, A, B, ~q1, ~q2, ~q4);  // AND_Gate
  and and_9 (and_9_out, A, ~q1, ~q2, q3, ~q4);  // AND_Gate
  and and_10 (and_10_out, A, ~q1, ~q2, ~q3, q4);  // AND_Gate
  and and_11 (and_11_out, ~A, B, ~q1, ~q2, q3);  // AND_Gate
  and and_12 (and_12_out, A, ~B, q1, ~q2, ~q3, ~q4);  // AND_Gate
  and and_13 (and_13_out, A, ~B, ~q1, q3, ~q4);  // AND_Gate
  and and_14 (and_14_out, A, ~q1, ~q2, q3, ~q4);  // AND_Gate
  and and_15 (and_15_out, ~A, B, ~q1, ~q2, q4);  // AND_Gate
  and and_16 (and_16_out, A, ~B, ~q2, ~q3, ~q4);  // AND_Gate
  and and_17 (and_17_out, ~A, B, ~q1, ~q2, ~q3);  // AND_Gate
  and and_18 (z1, ~A, B, ~q1, ~q2, ~q3, q4);  // AND_Gate
  and and_19 (z2, ~A, B, ~q1, ~q2, q3, ~q4);  // AND_Gate
  and and_20 (z3, ~A, B, ~q1, ~q2, q3, q4);  // AND_Gate
  and and_21 (and_21_out, ~A, B, ~q1, ~q2, ~q3, ~q4);  // AND_Gate
  and and_22 (and_22_out, ~A, B, ~q1, q2, ~q3, q4);  // AND_Gate
  and and_23 (and_23_out, A, ~B, ~q1, q2, ~q3, q4);  // AND_Gate
  and and_24 (and_24_out, A, B, ~q1, q2, ~q3, q4);  // AND_Gate
  and and_25 (and_25_out, A, ~B, ~q1, q2, q3, ~q4);  // AND_Gate
  and and_26 (and_26_out, A, ~B, ~q1, q2, q3, q4);  // AND_Gate
  and and_27 (and_27_out, A, ~B, q1, ~q2, ~q3, ~q4);  // AND_Gate
  and and_28 (and_28_out, ~A, B, ~q1, q2, q3, ~q4);  // AND_Gate
  and and_29 (and_29_out, ~A, B, ~q1, q2, q3, q4);  // AND_Gate
  and and_30 (and_30_out, ~A, B, q1, ~q2, ~q3, ~q4);  // AND_Gate
  and and_31 (and_31_out, A, ~B, ~q1, ~q2, q3, q4);  // AND_Gate
  and and_32 (and_32_out, A, B, ~q1, ~q2, q3, q4);  // AND_Gate
  and and_33 (and_33_out, ~A, B, ~q1, q2, ~q3, ~q4);  // AND_Gate
  and and_34 (and_34_out, A, ~B, ~q1, q2, ~q3, ~q4);  // AND_Gate
  and and_35 (and_35_out, A, B, ~q1, q2, ~q3, ~q4);  // AND_Gate
  not not_2 (not_2_out, not_1_out);
  or u_Q1 (Q1_out, and_1_out, and_2_out);
  or u_Q2 (Q2_out, and_3_out, and_4_out, and_5_out, and_6_out);
  or u_Q3 (Q3_out, and_7_out, and_8_out, and_9_out, and_10_out, and_11_out, and_12_out);
  or u_Q4 (Q4_out, and_13_out, and_14_out, and_15_out, and_16_out, and_17_out);
  or or_2 (z4, and_21_out, and_22_out, and_23_out, and_24_out);
  or or_3 (z5, and_25_out, and_26_out, and_27_out);
  or or_4 (z6, and_28_out, and_29_out, and_30_out);
  or or_5 (z7, and_31_out, and_32_out, and_33_out, and_34_out, and_35_out);
  D_Flip_Flop d_ff_1 (.clk(not_2_out), .D(Q1_out), .Q(q1_2));  // open: Qn, preset, en, reset
  D_Flip_Flop d_ff_2 (.clk(not_2_out), .D(Q2_out), .Q(q2_2));  // open: Qn, preset, en, reset
  D_Flip_Flop d_ff_3 (.clk(not_2_out), .D(Q3_out), .Q(q3_2));  // open: Qn, preset, en, reset
  D_Flip_Flop d_ff_4 (.clk(not_2_out), .D(Q4_out), .Q(q4_2));  // open: Qn, preset, en, reset
endmodule

// Fl
module automata_states (
  input  q1,
  input  q2,
  input  q3,
  input  q4,
  output l1,
  output l2,
  output l3,
  output l4,
  output l5,
  output l6
);

  wire and_1_out, and_2_out, and_3_out, and_4_out, and_5_out, and_6_out, and_8_out, and_9_out, and_10_out;

  and and_1 (and_1_out, ~q1, ~q2, ~q3, ~q4);  // AND_Gate
  and and_2 (and_2_out, ~q1, ~q2, ~q3, q4);  // AND_Gate
  and and_3 (and_3_out, ~q1, ~q2, ~q3, ~q4);  // AND_Gate
  and and_4 (and_4_out, ~q1, ~q2, q3, ~q4);  // AND_Gate
  and and_5 (and_5_out, ~q1, ~q2, ~q3, ~q4);  // AND_Gate
  and and_6 (and_6_out, ~q1, ~q2, q3, q4);  // AND_Gate
  and and_7 (l4, ~q1, q2, ~q3, ~q4);  // AND_Gate
  and and_8 (and_8_out, ~q1, q2, q3, ~q4);  // AND_Gate
  and and_9 (and_9_out, ~q1, q2, q3, q4);  // AND_Gate
  and and_10 (and_10_out, q1, ~q2, ~q3, ~q4);  // AND_Gate
  and and_11 (l6, ~q1, q2, ~q3, q4);  // AND_Gate
  or or_1 (l1, and_1_out, and_2_out);
  or or_2 (l2, and_3_out, and_4_out);
  or or_3 (l3, and_5_out, and_6_out);
  or or_4 (l5, and_8_out, and_9_out, and_10_out);
endmodule

// SW
module stopwatch (
  input  state,
  input  generator,
  input  start_pause,
  input  reset,
  output [3:0] out_5,
  output [3:0] out_6,
  output [3:0] out_7,
  output [3:0] out_8
);

  wire and_1_out, and_2_out, and_3_out, and_4_out, controlled_buffer_4_out, or_1_out, or_2_out, or_3_out,
       or_4_out, t_ff_1_q;
  wire [3:0] controlled_buffer_1_out, controlled_buffer_2_out, controlled_buffer_3_out,
       controlled_buffer_5_out, counter_1_q, counter_2_q, counter_3_q, counter_4_q;

  Counter #(.width(4), .max('hf)) counter_1 (
    .Q(counter_1_q), .clk(and_2_out), .clr(or_1_out));  // open: load, D, count, carry
  or or_1 (or_1_out, reset, and_1_out);
  assign controlled_buffer_1_out = state ? counter_1_q : 4'bz;  // Controlled_Buffer controlled_buffer_1
  and and_1 (and_1_out, counter_1_q[1], counter_1_q[2]);
  or or_2 (or_2_out, and_2_out, reset);
  Counter #(.width(4), .max('hf)) counter_2 (
    .Q(counter_2_q), .clk(and_3_out), .clr(or_2_out));  // open: load, D, count, carry
  assign controlled_buffer_2_out = state ? counter_2_q : 4'bz;  // Controlled_Buffer controlled_buffer_2
  and and_2 (and_2_out, counter_2_q[1], counter_2_q[3]);
  Counter #(.width(4), .max('hf)) counter_3 (
    .Q(counter_3_q), .clk(and_4_out), .clr(or_3_out));  // open: load, D, count, carry
  or or_3 (or_3_out, reset, and_3_out);
  assign controlled_buffer_3_out = state ? counter_3_q : 4'bz;  // Controlled_Buffer controlled_buffer_3
  and and_3 (and_3_out, counter_3_q[1], counter_3_q[2]);
  T_Flip_Flop t_ff_1 (.clk(start_pause), .T(1'b1), .Q(t_ff_1_q));  // open: Qn, preset, reset, en
  Counter #(.width(4), .max('hf)) counter_4 (
    .Q(counter_4_q), .clk(controlled_buffer_4_out), .clr(or_4_out));  // open: load, D, count, carry
  assign controlled_buffer_4_out = t_ff_1_q ? generator : 1'bz;  // Controlled_Buffer controlled_buffer_4
  or or_4 (or_4_out, reset, and_4_out);
  assign controlled_buffer_5_out = state ? counter_4_q : 4'bz;  // Controlled_Buffer controlled_buffer_5
  and and_4 (and_4_out, counter_4_q[1], counter_4_q[3]);
  Multiplexer #(.width(4)) multiplexer_1 (
    .in0(4'b0000), .in1(controlled_buffer_1_out), .out(out_5), .sel(state));  // open: en
  Multiplexer #(.width(4)) multiplexer_2 (
    .in0(4'b0000), .in1(controlled_buffer_2_out), .out(out_6), .sel(state));  // open: en
  Multiplexer #(.width(4)) multiplexer_3 (
    .in0(4'b0000), .in1(controlled_buffer_3_out), .out(out_7), .sel(state));  // open: en
  Multiplexer #(.width(4)) multiplexer_4 (
    .in0(4'b0000), .in1(controlled_buffer_5_out), .out(out_8), .sel(state));  // open: en

  // Other names for the same wires on the sheet: st = state

  // Notes on the sheet:
  //   out_7: pull=down
  //   out_8: pull=down
  //   out_6: pull=down
  //   out_5: pull=down
endmodule

// SIG
module signal (
  input  [3:0] sec_units,
  input  [3:0] sec_tens,
  input  [3:0] min_units,
  input  [3:0] min_tens,
  output out_5
);

  wire comparator_1_eq, comparator_1_gt, comparator_2_eq, comparator_2_lt, comparator_3_eq, comparator_4_eq,
       comparator_5_eq, or_1_out, or_2_out;

  Comparator #(.width(4)) comparator_1 (
    .a(sec_units), .b(4'b0000), .gt(comparator_1_gt), .eq(comparator_1_eq));  // open: lt
  or or_1 (or_1_out, comparator_1_gt, comparator_1_eq);
  Comparator #(.width(4)) comparator_2 (
    .a(sec_units), .b(4'b0100), .eq(comparator_2_eq), .lt(comparator_2_lt));  // open: gt
  or or_2 (or_2_out, comparator_2_eq, comparator_2_lt);
  Comparator #(.width(4)) comparator_3 (.a(sec_tens), .b(4'b0000), .eq(comparator_3_eq));  // open: gt, lt
  Comparator #(.width(4)) comparator_4 (.a(min_units), .b(4'b0000), .eq(comparator_4_eq));  // open: gt, lt
  Comparator #(.width(4)) comparator_5 (.a(min_tens), .b(4'b0000), .eq(comparator_5_eq));  // open: gt, lt
  and and_1 (out_5, or_1_out, or_2_out, comparator_3_eq, comparator_4_eq, comparator_5_eq);
endmodule
